# Fritzing sketch pir (saved by Fritzing 0.8.7b)
breadboards: 1

parts:
  元件3 = Arduino Mega 2560 (Rev3)
  R1 = Resistor [tolerance=±5% resistance=220 package=THT]  # not connected
  LED1 = LED - 5mm [color="Red (633nm)" package="5 mm [THT]"]

nets:
  N1: 元件3.GND, LED1.cathode
